# Fritzing sketch Untitled Sketch (saved by Fritzing 0.9.9b)

parts:
  Part1 = HC-05 [part_number=HC-05 package="breakout board"]
  DHT1 = DHT11 Humitidy and Temperature Sensor
  KF-1 = KF-301 Relay [package=THT]
  BULB1 = Incandescent light bulb small [package="bulb sm"]
  U1 = NodeMCU V1.0
  JACK1 = 2.1mm Barrel Jack with Terminal Block
  LED1 = LED - 3mm [color="Red (633nm)" current=0.030 package="3 mm [THT]"]

nets:
  VCC: Part1.VCC, DHT1.VDD, KF-1.power, U1.3V3
  GND: Part1.GND, DHT1.GND, KF-1.ground, U1.GND, LED1.cathode
  N1: Part1.TXD, U1.D7
  N2: Part1.RXD, U1.D6
  N3: DHT1.NULL, U1.D5
  N4: KF-1.signal, U1.D4
  N5: KF-1.C, JACK1.POS
  N6: KF-1.NO, BULB1.2
  N7: BULB1.1, JACK1.NEG
  N8: U1.D3, LED1.anode

custom parts:
  HC-05: A commonly available HC-05 Bluetooth breakout board.
  DHT11 Humitidy and Temperature Sensor: DHT11 Humidity and Temperature Sensor
  KF-301 Relay: KF-301
  NodeMCU V1.0: ESP8266 based NodeMCU
